# Fritzing sketch Tiny Board (saved by Fritzing 0.9.3b)
circuit board: 2.5cm x 2.5cm
breadboards: 1

parts:
  BATT = Battery Holders [package=battcom_20mm_pth]
  TINY_85 = IC, DIP package, 8 pins [chip_label=IC]
  I/O = Toggle Switch [package=THT]
  U1 = GAS_SENSOR [package=mq-3]
  Piezo = Piezo Speaker

nets:
  N1: BATT.+, I/O.L1, U1.A1, U1.H1
  N2: BATT.-, TINY_85.pin4, U1.H2, Piezo.pin2
  N3: TINY_85.pin6, Piezo.pin1
  N4: TINY_85.pin7, U1.B1
  N5: TINY_85.pin8, I/O.COM, I/O.L2
