# Fritzing sketch Yilime (saved by Fritzing 0.9.3b)
circuit board: 5.35033cm x 5.03772cm
breadboards: 3

parts:
  BTN = Momentary Switch [package=ksa_sealed_tac_switch]
  U2 = LIPO-2000mAh [package=lipo-2000]  # not connected
  PWR = Adafruit Pro Trinket LiIon/LiPoly Backpack [part_number="Adafruit #2124"]  # not connected
  JOY = Adafruit Analog 2-Axis Joystick [part_number="Adafruit #512"]  # not connected
  Part2 = TFT 2.2 inch 320x240 w microSD [part_number=1480]  # not connected
  Arduino = Arduino Pro Mini v13
  TOG = Toggle Switch [package=THT]
  JOY_- = female pin header, 5 pins [form="♀ (female)"]
  10K = Resistor [tolerance=±5% resistance=1k package=THT]
  +PZO- = Piezo Speaker
  Scr_9 = female pin header, 9 pins [form="♀ (female)"]
  DOF+ = female pin header, 6 pins [form="♀ (female)"]
  BAT_+ = female pin header, 2 pins [form="♀ (female)"]
  10k = Resistor [tolerance=±5% resistance=220 package=THT]
  RNeo_+_DO = female pin header, 4 pins [form="♀ (female)"]
  +LNeo- = female pin header, 4 pins [form="♀ (female)"]
  PWR_NEO_- = female pin header, 4 pins [form="♀ (female)"]

nets:
  N1: BTN.1, Arduino.D2
  N2: BTN.2, Arduino.VCC, JOY_-.pin2, Scr_9.pin8, DOF+.pin6, 10k.Pin_1
  N3: BTN.3, 10K.Pin_1
  N4: Arduino.A4, DOF+.pin4
  N5: Arduino.A5, DOF+.pin3
  N6: Arduino.RAW, TOG.COM
  N7: Arduino.GND, JOY_-.pin1, 10K.Pin_0, +PZO-.pin2, Scr_9.pin2, DOF+.pin5, BAT_+.pin2, RNeo_+_DO.pin1, +LNeo-.pin1, PWR_NEO_-.pin1
  N8: Arduino.A3, JOY_-.pin3
  N9: Arduino.A2, JOY_-.pin4
  N10: Arduino.D13/SCK, Scr_9.pin7
  N11: Arduino.D12/MISO, Scr_9.pin9
  N12: Arduino.D11_PWM/MOSI, Scr_9.pin6
  N13: Arduino.D10_PWM/SS, Scr_9.pin3
  N14: Arduino.D9_PWM, Scr_9.pin5
  N15: Arduino.D8, Scr_9.pin4
  N16: Arduino.D7, DOF+.pin1
  N17: Arduino.D6_PWM, +PZO-.pin1
  N18: Arduino.D5_PWM, RNeo_+_DO.pin2
  N19: Arduino.D4, JOY_-.pin5, 10k.Pin_0
  N20: TOG.L1, BAT_+.pin1
  N21: Scr_9.pin1, RNeo_+_DO.pin3, +LNeo-.pin3, PWR_NEO_-.pin3
  N22: RNeo_+_DO.pin4, PWR_NEO_-.pin2
  N23: +LNeo-.pin2, PWR_NEO_-.pin4

custom parts:
  Adafruit Pro Trinket LiIon/LiPoly Backpack: If you have a Pro Trinket you probably know it's the perfect little size for a portable project. This LiPoly backpack makes it really easy to do! Instead of wiring 2 or 3 boards together to make a charging system, this little PCB sits on top of the Pro Trinket and allows a LiPoly/LiIon battery to plug in. When the Pro Trinket USB port is powered, the battery is recharged automatically. Unplug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
  Adafruit Analog 2-Axis Joystick: This mini-kit makes it easy to mount a PSP/Xbox-like thumb joystick to your project. The thumbstick is an analog joystick - more accurate and sensitive than just 'directional' joysticks - with a 'press in to select' button. Since it's analog, you'll need two analog reading pins on your microcontroller to determine X and Y. Having an extra digital input will let you read the switch. The pack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
  TFT 2.2 inch 320x240 w microSD: This lovely little display breakout is the best way to add a small, colorful and bright display to any project. Since the display uses 4-wire SPI to communicate and has its own pixel-addressable frame buffer, it can be used with every kind of microcontroller. Even a very small one with low memory and few pins available! The 2.2" display has 320x240 color pixels.
